# Fritzing sketch Schema_Electrique (saved by Fritzing 0.9.9b)
breadboards: 1

parts:
  Raspberry_Pi = Raspberry Pi 4B
  Moteur_1 = DC Motor
  Moteur_2 = DC Motor
  Moteur = L293D [package=THT]
  VCC1 = Battery block 9V
  Capteur_de_Ligne = TCRT5000 sensor module [part_number=151608]
  Capteur_de_Ligne1 = TCRT5000 sensor module [part_number=151608]
  Capteur_de_Ligne2 = TCRT5000 sensor module [part_number=151608]
  Capteur_de_Ligne3 = TCRT5000 sensor module [part_number=151608]
  Capteur_Distance = HC-SR04 Ultrasonic Distance Sensor  # not connected
  Active_Buzzer = Buzzer 12mm [package=buzzer-ccv]

nets:
  N1: Raspberry_Pi.3V3, Capteur_de_Ligne.T+, Capteur_de_Ligne1.T+, Capteur_de_Ligne2.T+, Capteur_de_Ligne3.T+
  N2: Raspberry_Pi.GND, Capteur_de_Ligne.T-, Capteur_de_Ligne1.T-, Capteur_de_Ligne2.T-, Capteur_de_Ligne3.T-, Active_Buzzer.2
  N3: Raspberry_Pi.GPIO17, Moteur.In_4
  N4: Raspberry_Pi.GPIO18, Active_Buzzer.1
  N5: Raspberry_Pi.GPIO27, Moteur.In_3
  N6: Raspberry_Pi.GPIO22, Capteur_de_Ligne.D-
  N7: Raspberry_Pi.GPIO23, Moteur.In_1
  N8: Raspberry_Pi.GPIO24, Moteur.In_2
  N9: Raspberry_Pi.GPIO5, Capteur_de_Ligne1.D-
  N10: Raspberry_Pi.GPIO6, Capteur_de_Ligne3.D-
  N11: Raspberry_Pi.GPIO12, Moteur.Enable_1
  N12: Raspberry_Pi.GPIO13, Moteur.Enable_2
  N13: Raspberry_Pi.GPIO16, Capteur_de_Ligne2.D-
  N14: Moteur_1.pin_1, Moteur.Out_1_(_Controlled_by_Enable_1_)
  N15: Moteur_1.pin_2, Moteur.Out_2_(_Controlled_by_Enable_1_)
  N16: Moteur_2.pin_1, Moteur.Out_4_(_Controlled_by_Enable_2_)
  N17: Moteur_2.pin_2, Moteur.Out_3_(_Controlled_by_Enable_2_)
  N18: Moteur.0V, VCC1.+
  N19: Moteur.+Vmotor, VCC1.-

custom parts:
  TCRT5000 sensor module: breakout board with TCRT5000
