# Fritzing sketch Schéma_2 (saved by Fritzing 0.9.9b)
breadboards: 1

parts:
  Moteur_1 = DC Motor
  Moteur_2 = DC Motor
  Moteur = L293D [package=THT]
  VCC1 = Battery block 9V
  Active_Buzzer = Buzzer 12mm [package=buzzer-ccv]  # not connected
  LCM1602_IIC2 = LCM1602 IIC [part_number="LCM1602 IIC" chip_label="LCM1602 IIC" package="DIP (Dual Inline) [THT]"]  # not connected
  Mod1 = Raspberry Pi 4B  # not connected
  Part2 = Adafruit TCS34725 RGB Color Sensor [part_number="Adafruit #1334"]  # not connected
  Capteur_de_Ligne1 = TCRT5000 sensor module [part_number=151608]
  Capteur_de_Ligne2 = TCRT5000 sensor module [part_number=151608]
  Capteur_de_Ligne3 = TCRT5000 sensor module [part_number=151608]
  Capteur_de_Ligne4 = TCRT5000 sensor module [part_number=151608]
  Capteur_de_Ligne5 = TCRT5000 sensor module [part_number=151608]

nets:
  N1: Moteur_1.pin_1, Moteur.Out_1_(_Controlled_by_Enable_1_)
  N2: Moteur_1.pin_2, Moteur.Out_2_(_Controlled_by_Enable_1_)
  N3: Moteur_2.pin_1, Moteur.Out_4_(_Controlled_by_Enable_2_)
  N4: Moteur_2.pin_2, Moteur.Out_3_(_Controlled_by_Enable_2_)
  N5: Moteur.0V, VCC1.+
  N6: Moteur.+Vmotor, VCC1.-
  N7: Capteur_de_Ligne1.T-, Capteur_de_Ligne2.T-, Capteur_de_Ligne3.T-, Capteur_de_Ligne4.T-, Capteur_de_Ligne5.T-
  N8: Capteur_de_Ligne2.T+, Capteur_de_Ligne3.T+, Capteur_de_Ligne4.T+, Capteur_de_Ligne5.T+

custom parts:
  LCM1602 IIC: I2C-Module to use a 1602 or 2004 LCD on with the wire.h libory Serial LCD Modul
  Adafruit TCS34725 RGB Color Sensor: Your electronics can now see in dazzling color with this lovely color light sensor. We found the best color sensor on the market, the TCS34725, which has RGB and Clear light sensing elements. An IR blocking filter, integrated on-chip and localized to the color sensing photodiodes, minimizes the IR spectral component of the incoming light and allows color measurements to be made accurately. The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
  TCRT5000 sensor module: breakout board with TCRT5000
